# Fritzing sketch ricevitore go kart circuito (saved by Fritzing 0.9.3b)

parts:
  BAT1 = 18650 battery holder [package=battery-18650-kit]
  BAT2 = 18650 battery holder [package=battery-18650-kit]
  U1 = LM2596 step down module
  Componente1 = Arduino Uno (Rev3)
  Componente2 = Arduino Mega ADK (Rev3)
  U4 = 2-Channel 5v Relay Shield [package=relay-2ch5v10a]
  M1 = DC Motor
  M2 = DC Motor
  BAT3 = 18650 battery holder [package=battery-18650-kit]
  BAT4 = 18650 battery holder [package=battery-18650-kit]
  BAT5 = 18650 battery holder [package=battery-18650-kit]
  U5 = SWITCH_SPDT [package=kps-1290]
  Componente3 = NRF24L01+ Breakout Board
  U6 = 4-Channel 5v Relay Shield [package=relay-4ch5v10a]
  U7 = 4-Channel 5v Relay Shield [package=relay-4ch5v10a]
  R1 = Resistor [tolerance=±5% resistance=100k package=THT]
  R2 = Resistor [tolerance=±5% resistance=100k package=THT]
  R3 = Resistor [tolerance=±5% resistance=100k package=THT]
  R4 = Resistor [tolerance=±5% resistance=100k package=THT]
  R5 = Resistor [tolerance=±5% resistance=100k package=THT]
  R6 = Resistor [tolerance=±5% resistance=100k package=THT]
  R7 = Resistor [tolerance=±5% resistance=100k package=THT]
  R8 = Resistor [tolerance=±5% resistance=100k package=THT]
  R9 = Resistor [tolerance=±5% resistance=100k package=THT]
  C1 = Electrolytic Capacitor [capacitance=4µF voltage=50V package="100 mil [THT, electrolytic]"]
  avanti_go_kart = Pushbutton [package="[THT]"]
  destra_go_kart1 = Pushbutton [package="[THT]"]
  sinistra_go_kart2 = Pushbutton [package="[THT]"]

nets:
  N1: BAT1.+, U5.P
  N2: BAT1.-, BAT2.+
  GND: BAT2.-, U1.IN-, U1.OUT-, Componente1.GND, Componente2.GND, U4.GND, Componente3.GND, U6.GND, U7.GND, C1.-, avanti_go_kart.Pin_3, avanti_go_kart.Pin_4, destra_go_kart1.Pin_4, sinistra_go_kart2.Pin_3, sinistra_go_kart2.Pin_4
  VIN: U1.IN+, Componente1.VIN, Componente2.VIN, U5.S
  VCC: U1.OUT+, U4.VCC, U6.VCC, U7.VCC, R1.Pin_1, R2.Pin_1, R3.Pin_1, R4.Pin_1, R5.Pin_1, R6.Pin_1, R7.Pin_1, R8.Pin_1, R9.Pin_1
  N3: Componente1.D8, Componente2.A5
  N4: Componente1.D9_PWM, Componente3.CE
  N5: Componente1.D10_PWM/SS, Componente3.CS
  N6: Componente1.D11_PWM/MOSI, Componente3.MOSI
  N7: Componente1.D12/MISO, Componente3.MISO
  N8: Componente1.D13/SCK, Componente3.SCK
  N9: Componente1.D3_PWM, Componente2.A0
  N10: Componente1.D4, Componente2.A1
  N11: Componente1.D5_PWM, Componente2.A2
  N12: Componente1.D6_PWM, Componente2.A3
  N13: Componente1.D7, Componente2.A4
  3V3: Componente1.3V3, Componente3.VCC, C1.+
  N14: Componente2.A8, sinistra_go_kart2.Pin_1, sinistra_go_kart2.Pin_2
  N15: Componente2.A6, avanti_go_kart.Pin_1, avanti_go_kart.Pin_2
  N16: Componente2.A7, destra_go_kart1.Pin_1, destra_go_kart1.Pin_2
  N17: Componente2.D11_PWM, U4.IN1, R9.Pin_0
  N18: Componente2.D10_PWM, U7.IN4, R8.Pin_0
  N19: Componente2.D9_PWM, U7.IN3, R7.Pin_0
  N20: Componente2.D8_PWM, U7.IN2, R6.Pin_0
  N21: Componente2.D3_PWM, U6.IN1, R1.Pin_0
  N22: Componente2.D4_PWM, U6.IN2, R2.Pin_0
  N23: Componente2.D5_PWM, U6.IN3, R3.Pin_0
  N24: Componente2.D6_PWM, U6.IN4, R4.Pin_0
  N25: Componente2.D7_PWM, U7.IN1, R5.Pin_0
  N26: U4.K1-In, M1.pin_2, U6.K2-In, U7.K3-In
  N27: U4.K1-Off, M2.pin_1, U6.K3-In, U7.K2-In
  N28: U4.K1-On, U4.K2-On
  N29: M1.pin_1, U6.K1-In, U7.K1-In
  N30: M2.pin_2, U6.K4-In, U7.K4-In
  N31: BAT3.+, U6.K1-Off, U6.K3-Off, U7.K3-Off, U7.K4-Off
  N32: BAT3.-, BAT4.+
  N33: BAT4.-, BAT5.+
  N34: BAT5.-, U6.K2-Off, U6.K4-Off, U7.K1-Off, U7.K2-Off

custom parts:
  18650 battery holder: 18650 Battery Holder
  LM2596 step down module: LM2596 DC-DC step down power supply module 3 A.
  2-Channel 5v Relay Shield: 2 Channel 5v Relay Shield w. 2x SPD-06VDC-SD-C
  4-Channel 5v Relay Shield: 4 Channel 5v Relay Shield w. 2x SPD-06VDC-SD-C
